# Fritzing sketch wiring (saved by Fritzing 0.9.5d)

parts:
  Digispark1 = Digispark
  LED1 = LED - 5mm [color="Red (633nm)" package="5 mm [THT]"]
  LED2 = LED - 5mm [color="Green (570nm)" package="5 mm [THT]"]
  R1 = Resistor [tolerance=±5% resistance=150 package=THT]
  R2 = Resistor [tolerance=±5% resistance=150 package=THT]

nets:
  N1: Digispark1.GND, LED1.cathode, LED2.cathode
  N2: Digispark1.P1, R1.Pin_0
  N3: Digispark1.P2, R2.Pin_0
  N4: LED1.anode, R1.Pin_1
  N5: LED2.anode, R2.Pin_1

custom parts:
  Digispark: The Digispark is an Attiny85 based microcontroller development board similar to the Arduino line, only cheaper, smaller, and a bit less powerful. With a whole host of shields to extend its functionality and the ability to use the familiar Arduino IDE the Digispark is a great way to jump into electronics, or perfect for when an Arduino is too big or too much.
